# Fritzing sketch shema arduino morse (saved by Fritzing 0.9.10b)
breadboards: 1

parts:
  Composant1 = Arduino Uno (Rev3)
  LED1 = LED - 5mm [color="Yellow (595nm)" current=0.030 package="5 mm [THT]"]
  R1 = Resistor [tolerance=±5% power=0.25 resistance=220 package=THT]
  J1 = Piezo Speaker
  LED2 = LED - 5mm [color="Red (633nm)" current=0.030 package="5 mm [THT]"]
  R2 = Resistor [tolerance=±5% power=0.25 resistance=220 package=THT]

nets:
  N1: Composant1.D2, LED2.anode, R2.Pin_0, R2.Pin_1
  N2: Composant1.D4, J1.pin2
  N3: Composant1.D5_PWM, LED1.anode, R1.Pin_0, R1.Pin_1
  N4: Composant1.5V, LED1.cathode
  N5: Composant1.GND, J1.pin1, LED2.cathode
